# Fritzing sketch Centrifuge-Fritzing (saved by Fritzing 0.9.3b)
breadboards: 2

parts:
  S1_Power_Switch = Pushbutton [package=THT]
  Power_plug1_-_12V = Power plug
  U1_-_ESC_control = mystery part, 3 pins [chip_label="ESC C" spacing=300mil]
  U2_-_ESC_power = mystery part, 2 pins [chip_label=ESC spacing=300mil]
  U3_-_Infrared = mystery part, 4 pins [chip_label=Infrared spacing=300mil]
  R1_-_220 = Resistor [tolerance=±5% resistance=220 package=THT]
  R2_-_6_8K = Resistor [tolerance=±5% resistance=6.8k package=THT]
  U1 = mystery part, 4 pins [chip_label=I2C spacing=300mil]
  R1_-_Rotary_encoder = Rotary Potentiometer (Small) [maximum_resistance=100kΩ package=THT]
  LCD1 = LCD screen  # not connected
  Arduino1 = Arduino Uno (Rev3)
  S1 = Pushbutton [package="[THT]"]
  R1 = Resistor [tolerance=±5% resistance=1k package=THT]

nets:
  N1: S1_Power_Switch.leg0, Power_plug1_-_12V.VCC
  N2: S1_Power_Switch.leg1, U2_-_ESC_power.pin2
  N3: Power_plug1_-_12V.GND, U2_-_ESC_power.pin1
  N4: U1_-_ESC_control.pin1, U3_-_Infrared.pin2, U1.pin4, R1_-_Rotary_encoder.wiper, Arduino1.GND, R1.Pin_1
  N5: U1_-_ESC_control.pin2, R1_-_220.Pin_0, R2_-_6_8K.Pin_1, U1.pin3, Arduino1.VIN, S1.Pin_3, S1.Pin_4
  N6: U1_-_ESC_control.pin3, Arduino1.D9_PWM
  N7: U3_-_Infrared.pin1, R2_-_6_8K.Pin_0, Arduino1.D6_PWM
  N8: U3_-_Infrared.pin3, R1_-_220.Pin_1
  N9: U1.pin1, Arduino1.A5/SCL
  N10: U1.pin2, Arduino1.A4/SDA
  N11: R1_-_Rotary_encoder.leg1, Arduino1.D2
  N12: R1_-_Rotary_encoder.leg2, Arduino1.D3_PWM
  N13: Arduino1.D12/MISO, S1.Pin_1, S1.Pin_2, R1.Pin_0

notes:
  LCD I2C interface:
  SCL - A5
  SDA - A4
  Vcc
  Gnd
  ESC signal
  Rotary Encoder
  Infrared RPM sensor
  Power switch
  12V power supply
  ESC power
  Push Button
  12 V Power Supply
  Power Switch
  ESC Power Connector
  Push button
  The ESC is a 5V source
  1 is GND, 2 = Vcc, 3 = signal
  Infrared sensor
  Rotary encoder
  The LCD has an I2C interface
  The Arduino gets power from the ESC
  via these lines
